# Fritzing sketch 블루투스 RC카 (saved by Fritzing 0.9.10b)
breadboards: 1

parts:
  S1 = H-Bridge with L298N
  M2 = DC Motor [voltage_(max)=6V voltage_(min)=3V]
  M3 = DC Motor [voltage_(max)=6V voltage_(min)=3V]
  부품1 = Bluetooth HM-10
  부품2 = Arduino Uno (Rev3)
  HC-SR04_Sensor_1 = HC-SR04 Ultrasonic Distance Sensor
  HC-SR04_Sensor_2 = HC-SR04 Ultrasonic Distance Sensor
  LED1 = LED - 5mm [color="Yellow (595nm)" current=0.030 package="5 mm [THT]"]
  LED2 = LED - 5mm [color="Yellow (595nm)" current=0.030 package="5 mm [THT]"]
  LED3 = LED - 5mm [color="Yellow (595nm)" current=0.030 package="5 mm [THT]"]
  LED4 = LED - 5mm [color="Yellow (595nm)" current=0.030 package="5 mm [THT]"]
  VCC1 = Battery
  J1 = Piezo Speaker

nets:
  N1: S1.12V, VCC1.+
  N2: S1.GND, VCC1.-
  N3: S1.ENA, 부품2.D8
  N4: S1.IN1, 부품2.D4
  N5: S1.IN2, 부품2.D5_PWM
  N6: S1.IN3, 부품2.D6_PWM
  N7: S1.IN4, 부품2.D7
  N8: S1.ENB, 부품2.D9_PWM
  N9: S1.M1-01, M3.pin_1
  N10: S1.M1-02, M3.pin_2
  N11: S1.M2-01, M2.pin_2
  N12: S1.M2-02, M2.pin_1
  N13: 부품1.RXD, 부품2.D3_PWM
  N14: 부품1.TXD, 부품2.D2
  GND: 부품1.GND, HC-SR04_Sensor_1.GND, LED1.cathode, LED2.cathode
  VCC: 부품1.VCC, HC-SR04_Sensor_1.VCC
  N15: 부품2.A0, LED1.anode, LED4.anode
  N16: 부품2.A1, LED2.anode, LED3.anode
  N17: 부품2.A2, J1.pin2
  N18: 부품2.D10_PWM/SS, HC-SR04_Sensor_1.TRIG
  N19: 부품2.D11_PWM/MOSI, HC-SR04_Sensor_1.ECHO
  N20: 부품2.D12/MISO, HC-SR04_Sensor_2.TRIG
  N21: 부품2.D13/SCK, HC-SR04_Sensor_2.ECHO
  5V: 부품2.5V, HC-SR04_Sensor_2.VCC
  GND_2: 부품2.GND, HC-SR04_Sensor_2.GND, LED3.cathode, LED4.cathode, J1.pin1

custom parts:
  H-Bridge with L298N: h-bridge
