# Fritzing sketch Save AR10_4LED (saved by Fritzing 0.9.3b)
breadboards: 1

parts:
  부품1 = Arduino Uno (Rev3)
  LED1 = LED - 5mm [color="Green (555nm)" package="5 mm [THT]"]
  LED2 = LED - 5mm [color="Blue (470nm)" package="5 mm [THT]"]
  R1 = Resistor [tolerance=±5% resistance=220 package=THT]  # not connected
  R2 = Resistor [tolerance=±5% resistance=220 package=THT]  # not connected
  LED3 = LED - 5mm [color="Red (633nm)" package="5 mm [THT]"]
  R3 = Resistor [tolerance=±5% resistance=220 package=THT]  # not connected
  R4 = Resistor [tolerance=±5% resistance=220 package=THT]  # not connected
  R5 = Resistor [tolerance=±5% resistance=220 package=THT]
  R6 = Resistor [tolerance=±5% resistance=220 package=THT]
  LED4 = LED - 5mm [color="Yellow (585nm)" package="5 mm [THT]"]

nets:
  N1: 부품1.D10_PWM/SS, LED4.anode
  N2: 부품1.D3_PWM, LED3.anode
  N3: 부품1.D5_PWM, LED1.anode
  N4: 부품1.D6_PWM, LED2.anode
  N5: 부품1.GND, R5.Pin_1, R6.Pin_1
  N6: LED3.cathode, R5.Pin_0
  N7: R6.Pin_0, LED4.cathode
